# Fritzing sketch llm-wiring-diagram-v01 (saved by Fritzing 1.0.8)
breadboards: 1

parts:
  LED1 = LED - 5mm [color="Red (633nm)" current=0.030A package="5 mm [THT]"]
  R1 = Resistor [tolerance=±5% resistance=220 package="0402 [SMD]"]
  BUTTON1 = Arcade Button (white)
  J1 = screw terminal, 5 pins
  ADC1 = MCP3008 [package=dil16]
  J2 = screw terminal, 5 pins
  J3 = screw terminal, 5 pins
  J5 = screw terminal, 5 pins
  R2 = Rotary Potentiometer (Small) [maximum_resistance=100kΩ knob_status=50% power=0.5W package=THT]
  J6 = screw terminal, 5 pins
  Mod2 = Raspberry Pi 4B

nets:
  N1: LED1.cathode, BUTTON1.COM, J1.pin5, ADC1.DGND, ADC1.AGND, J2.pin1, J5.pin1, J5.pin2, J5.pin3, J5.pin4, J5.pin5, R2.leg2, Mod2.GND
  N2: LED1.anode, R1.Pin_1
  N3: R1.Pin_0, Mod2.GPIO23
  N4: BUTTON1.NO, Mod2.GPIO24
  N5: J1.pin1, ADC1.CLK, Mod2.GPIO11_(SCLK)
  N6: J1.pin2, ADC1.Dout, Mod2.GPIO9_(MISO)
  N7: J1.pin3, ADC1.Din, Mod2.GPIO10_(MOSI)
  N8: J1.pin4, ADC1.CS/SHDN, Mod2.GPIO8_(CE0)
  N9: ADC1.CH0, R2.wiper, J6.pin5
  N10: ADC1.CH1, J6.pin4
  N11: ADC1.CH2, J6.pin3
  N12: ADC1.CH3, J6.pin2
  N13: ADC1.CH4, J6.pin1
  VDD: ADC1.VREF, ADC1.VDD, J2.pin2, J2.pin3, J3.pin1, J3.pin2, J3.pin3, J3.pin4, J3.pin5, R2.leg1, Mod2.3V3

custom parts:
  Arcade Button (white): Adafruit Arcade Button (white)
  Raspberry Pi 4B: The RPi4B, a faster version of the awesome Raspberry Pi 3 ARM Board with 40 pin gpio. Ready for special Raspberry Pi B+ and RPi2 Hat (Hardware attached (on) top) new features: The most surprising change for the Pi 4B is that it is available with three different amounts of fast DDR4 SDRAM memory; 1GB, 2GB, or 4GB. Combined with a newer 1.5GHz quad-core processor, the Pi 4B can run larger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
